# Fritzing sketch Mega (saved by Fritzing 0.9.1b)
circuit board: 12cm x 5.64444cm
breadboards: 2

parts:
  Part1 = Arduino Mega 2560 (Rev3)
  Uzak-Trig = screw terminal, 4 pins
  Uzak_IR = screw terminal, 4 pins
  SG4 = Buzzer 12mm [package=buzzer-12mm-ns]
  Ekran_1 = screw terminal, 6 pins
  Ekran_2 = screw terminal, 6 pins
  Ekran_Isık = screw terminal, 2 pins
  Hareket-Ses = screw terminal, 3 pins
  Serial = screw terminal, 2 pins
  Servo = screw terminal, 2 pins
  TCRT = screw terminal, 2 pins
  LDR = screw terminal, 2 pins
  +_Uzaklık = screw terminal, 6 pins
  +_Ses_Hareket = screw terminal, 3 pins
  +_Ekran = screw terminal, 2 pins
  +_LDR = screw terminal, 2 pins
  +_TCRT = screw terminal, 2 pins
  +_Servo = screw terminal, 2 pins
  +_giris_uzaklık = screw terminal, 2 pins
  +_giris_servo = screw terminal, 2 pins
  +_giris_sensor = screw terminal, 2 pins
  GND = screw terminal, 2 pins
  SG5 = Buzzer 12mm [package=buzzer-12mm-ns]
  LED1 = LED - 5mm [color="Red (633nm)" package="5 mm [THT]"]
  LED2 = LED - 5mm [color="Red (633nm)" package="5 mm [THT]"]
  R2 = Resistor [tolerance=±5% resistance=100 package=THT]
  R3 = Resistor [tolerance=±5% resistance=100 package=THT]

nets:
  N1: Part1.A0, Uzak_IR.pin1
  N2: Part1.A1, Uzak_IR.pin2
  N3: Part1.A2, Uzak_IR.pin3
  N4: Part1.A3, Uzak_IR.pin4
  N5: Part1.A4, LDR.pin1
  N6: Part1.A5, LDR.pin2
  N7: Part1.A6, TCRT.pin1
  N8: Part1.A7, TCRT.pin2
  N9: Part1.GND, SG4.2, +_giris_uzaklık.pin2, +_giris_servo.pin2, +_giris_sensor.pin1, GND.pin1, GND.pin2, SG5.2, R2.Pin_0, R3.Pin_0
  N10: Part1.D11_PWM, Serial.pin1
  N11: Part1.D10_PWM, Serial.pin2
  N12: Part1.D9_PWM, LED2.anode
  N13: Part1.D8_PWM, LED1.anode
  N14: Part1.D6_PWM, Servo.pin2
  N15: Part1.D7_PWM, Servo.pin1
  N16: Part1.D22, Uzak-Trig.pin4
  N17: Part1.D23, Uzak-Trig.pin3
  N18: Part1.D24, Uzak-Trig.pin2
  N19: Part1.D25, Uzak-Trig.pin1
  N20: Part1.D26, Hareket-Ses.pin3
  N21: Part1.D28, Hareket-Ses.pin1
  N22: Part1.D29, Hareket-Ses.pin2
  N23: Part1.D30, SG4.1
  N24: Part1.D31, SG5.1
  N25: Part1.D32, Ekran_2.pin6
  N26: Part1.D33, Ekran_2.pin5
  N27: Part1.D34, Ekran_2.pin4
  N28: Part1.D35, Ekran_2.pin3
  N29: Part1.D36, Ekran_2.pin2
  N30: Part1.D37, Ekran_2.pin1
  N31: Part1.D38, Ekran_Isık.pin1
  N32: Part1.D39, Ekran_Isık.pin2
  N33: Part1.D40, Ekran_1.pin6
  N34: Part1.D41, Ekran_1.pin5
  N35: Part1.D42, Ekran_1.pin4
  N36: Part1.D43, Ekran_1.pin3
  N37: Part1.D44, Ekran_1.pin2
  N38: Part1.D45, Ekran_1.pin1
  N39: +_Uzaklık.pin1, +_Uzaklık.pin2, +_Uzaklık.pin3, +_Uzaklık.pin4, +_Uzaklık.pin5, +_Uzaklık.pin6, +_giris_uzaklık.pin1
  N40: +_Ses_Hareket.pin1, +_Ses_Hareket.pin2, +_Ses_Hareket.pin3, +_Ekran.pin1, +_Ekran.pin2, +_LDR.pin1, +_LDR.pin2, +_TCRT.pin1, +_TCRT.pin2, +_giris_sensor.pin2
  N41: +_Servo.pin1, +_Servo.pin2, +_giris_servo.pin1
  N42: LED1.cathode, R3.Pin_1
  N43: LED2.cathode, R2.Pin_1

notes:
  Servo
  LDR
  Uzaklık_IR
  TCRT
  BG
  Ekran
  Robotek Kulubu
  NO201
