# Fritzing sketch Uno (saved by Fritzing 0.9.1b)
circuit board: 6.9215cm x 5.33756cm
perfboards: 1

parts:
  Motor_Encoder = screw terminal, 4 pins
  R1 = Resistor [tolerance=±5% resistance=100 package=THT]
  R2 = Resistor [tolerance=±5% resistance=100 package=THT]
  Cikis_1 = screw terminal, 2 pins
  Cikis_2 = screw terminal, 2 pins
  Giris_1 = screw terminal, 2 pins
  Giris_2 = screw terminal, 2 pins
  Q2 = Basic FET N-Channel [package="TO220 [THT]"]
  Analog = screw terminal, 3 pins
  T1 = LM35 Temperature Sensor [package="TO92 [THT]"]
  Q1 = Basic FET N-Channel [package="TO220 [THT]"]
  Motor_PWM-DIR = screw terminal, 8 pins
  Part1 = Arduino Uno (Rev3)
  GND = screw terminal, 2 pins
  MOTOR_5V = screw terminal, 2 pins
  R3 = Resistor [tolerance=±5% resistance=220 package=THT]
  R4 = Resistor [tolerance=±5% resistance=220 package=THT]
  LED1 = LED - 5mm [color="Red (633nm)" package="5 mm [THT]"]
  LED2 = LED - 5mm [color="Red (633nm)" package="5 mm [THT]"]

nets (from the pcb view):
  N1: Motor_Encoder.pin1, Part1.A3
  N2: Motor_Encoder.pin2, Part1.A2
  N3: Motor_Encoder.pin3, Part1.A1
  N4: Motor_Encoder.pin4, Part1.A0
  GND: R1.Pin_0, R2.Pin_0, Analog.pin2, T1.GND, Part1.GND, GND.pin1, GND.pin2, MOTOR_5V.pin2
  N5: R1.Pin_1, Q1.gate, Part1.D13/SCK, R3.Pin_0, R4.Pin_0
  N6: R2.Pin_1, Q2.gate, Part1.D12/MISO
  N7: Cikis_1.pin1, Q2.drain
  N8: Cikis_1.pin2, Giris_2.pin2
  N9: Cikis_2.pin1, Q1.drain
  N10: Cikis_2.pin2, Giris_1.pin2
  N11: Giris_1.pin1, Q1.source
  N12: Giris_2.pin1, Q2.source
  N13: Analog.pin1, Part1.A4/SDA
  N14: Analog.pin3, T1.+Vs, Part1.5V, MOTOR_5V.pin1
  N15: T1.Vout, Part1.A5/SCL
  N16: Motor_PWM-DIR.pin1, Part1.D9_PWM
  N17: Motor_PWM-DIR.pin2, Part1.D8
  N18: Motor_PWM-DIR.pin3, Part1.D7
  N19: Motor_PWM-DIR.pin4, Part1.D6_PWM
  N20: Motor_PWM-DIR.pin5, Part1.D5_PWM
  N21: Motor_PWM-DIR.pin6, Part1.D4
  N22: Motor_PWM-DIR.pin7, Part1.D3_PWM
  N23: Motor_PWM-DIR.pin8, Part1.D2
  N24: Part1.D10_PWM/SS, LED1.anode
  N25: Part1.D11_PWM/MOSI, LED2.anode
  N26: R3.Pin_1, LED1.cathode
  N27: R4.Pin_1, LED2.cathode

notes:
  Motor PWM DIR
  Encoder
  TCRT
  LM35
  Cikis 1
  Giris 2
  GND
