# Fritzing sketch Guc Kontrol (saved by Fritzing 0.9.1b)
perfboards: 1

parts:
  U1 = Voltage Regulator - 5V [package="TO220 [THT]"]
  U2 = SWITCH_SPDT [package=kps-1290]
  9V_Giriş = screw terminal, 2 pins
  9V_Giriş_2 = screw terminal, 2 pins
  9V_Çıkış = screw terminal, 2 pins
  9V_Çıkış_2 = screw terminal, 2 pins
  9V_Çıkış_3 = screw terminal, 2 pins
  U3 = Voltage Regulator - 5V [package="TO220 [THT]"]
  U4 = SWITCH_SPDT [package=kps-1290]
  U5 = Voltage Regulator - 5V [package="TO220 [THT]"]
  U6 = SWITCH_SPDT [package=kps-1290]
  Motor_Power_Giriş = screw terminal, 4 pins
  Motor_Power_Çıkış = screw terminal, 2 pins
  U7 = SWITCH_SPDT [package=kps-1290]
  Motor_5V_Giriş = screw terminal, 2 pins
  Motor_5V_Çıkış = screw terminal, 2 pins
  U8 = Voltage Regulator - 5V [package="TO220 [THT]"]
  U9 = SWITCH_SPDT [package=kps-1290]
  9V_Giriş_3 = screw terminal, 2 pins
  3V_Giriş = screw terminal, 2 pins
  3V_Çıkış = screw terminal, 2 pins
  U10 = SWITCH_SPDT [package=kps-1290]
  R1 = Resistor [tolerance=±5% resistance=220 package=THT]
  R2 = Resistor [tolerance=±5% resistance=220 package=THT]
  LED1 = LED - 5mm [color="Red (633nm)" package="5 mm [THT]"]
  LED2 = LED - 5mm [color="Red (633nm)" package="5 mm [THT]"]
  LED = screw terminal, 2 pins
  GND = screw terminal, 2 pins

nets:
  N1: U1.input_voltage, U2.P
  N2: U1.output_voltage, 9V_Çıkış.pin1
  N3: U2.O, 9V_Giriş.pin2
  N4: 9V_Giriş.pin1, 9V_Çıkış.pin2
  N5: 9V_Giriş_2.pin1, 9V_Çıkış_2.pin2
  N6: 9V_Giriş_2.pin2, U4.O
  N7: 9V_Çıkış_2.pin1, U3.output_voltage
  N8: 9V_Çıkış_3.pin1, U5.output_voltage
  N9: 9V_Çıkış_3.pin2, 9V_Giriş_3.pin1, R2.Pin_0, GND.pin1
  N10: U3.input_voltage, U4.P
  N11: U5.input_voltage, U6.P
  N12: U6.O, 9V_Giriş_3.pin2
  N13: Motor_Power_Giriş.pin1, Motor_Power_Çıkış.pin2
  N14: Motor_Power_Giriş.pin2, Motor_Power_Giriş.pin3
  N15: Motor_Power_Giriş.pin4, U7.P
  N16: Motor_Power_Çıkış.pin1, U7.O
  N17: Motor_5V_Giriş.pin1, Motor_5V_Çıkış.pin2
  N18: Motor_5V_Giriş.pin2, U9.P
  N19: Motor_5V_Çıkış.pin1, U8.output_voltage
  N20: U8.input_voltage, U9.O
  N21: 3V_Giriş.pin1, U10.S
  N22: 3V_Giriş.pin2, 3V_Çıkış.pin1
  N23: 3V_Çıkış.pin2, U10.P
  N24: R1.Pin_1, LED2.cathode
  N25: R2.Pin_1, LED1.cathode
  N26: LED1.anode, LED.pin2
  N27: LED2.anode, LED.pin1
