# Fritzing sketch Mega (saved by Fritzing 0.9.1b)
perfboards: 1

parts:
  Servo_Giriş3 = Screw terminal - 2 pins [package=THT]
  Servo_Çıkış3 = screw terminal, 4 pins
  Sensor_Çıkış3 = screw terminal, 9 pins
  Buzzer_+_gaz = screw terminal, 3 pins
  Ekran = Screw terminal - 2 pins [package=THT]
  Uzaklık_Çıkış3 = screw terminal, 8 pins
  Sensor_Giriş3 = Screw terminal - 2 pins [package=THT]
  Uzaklık_Giriş3 = Screw terminal - 2 pins [package=THT]
  Sensor_GND3 = screw terminal, 9 pins
  R13 = Resistor [tolerance=±5% resistance=220 package=THT]
  R14 = Resistor [tolerance=±5% resistance=220 package=THT]
  R15 = Resistor [tolerance=±5% resistance=220 package=THT]
  R16 = Resistor [tolerance=±5% resistance=220 package=THT]
  LED10 = LED - 5mm [color="Red (633nm)" package="5 mm [THT]"]
  LED11 = LED - 5mm [color="Red (633nm)" package="5 mm [THT]"]
  T4 = LM35 Temperature Sensor [package="TO92 [THT]"]
  lm_35_+_LED = screw terminal, 3 pins
  JP1 = Header 1 [package=1x01_offset]  # not connected
  Gaz = Header 1 [package=1x01_offset]
  JP3 = Header 1 [package=1x01_offset]

nets:
  N1: Servo_Giriş3.pin2, Servo_Çıkış3.pin1, Servo_Çıkış3.pin3
  N2: Sensor_Çıkış3.pin1, Sensor_Çıkış3.pin9, Sensor_Giriş3.pin1, JP3.1
  N3: Sensor_Çıkış3.pin2, T4.+Vs
  N4: Buzzer_+_gaz.pin1, Gaz.1
  N5: Ekran.pin2, R14.Pin_0
  N6: Uzaklık_Çıkış3.pin7, Uzaklık_Giriş3.pin1
  N7: Sensor_GND3.pin1, Sensor_GND3.pin9
  N8: R13.Pin_1, R14.Pin_1
  N9: R15.Pin_0, LED10.cathode
  N10: R15.Pin_1, R16.Pin_1
  N11: R16.Pin_0, LED11.cathode
  N12: LED10.anode, lm_35_+_LED.pin1
  N13: LED11.anode, lm_35_+_LED.pin2
  N14: T4.Vout, lm_35_+_LED.pin3
