# Fritzing sketch Şarj İstasyonu Akü (saved by Fritzing 0.9.2b)
circuit board: 12.4306cm x 8.86442cm
breadboards: 5

parts:
  R25 = Resistor [tolerance=±5% resistance=220 package=THT]
  5V+ = Header 1 [package=1x01_offset]
  Q8 = NPN-Transistor [package="TO92 [THT]"]
  SD- = Header 1 [package=1x01_offset]
  LED10 = LED - 5mm [color="Red (633nm)" package="5 mm [THT]"]
  S6 = Pushbutton [package=THT]
  5V_Çıkış_Motor = screw terminal, 2 pins
  S7 = Toggle Switch [package=THT]
  5V_Çıkış = screw terminal, 2 pins
  C7 = Capacitor [package=cap-pth-small2]
  12 = Voltage Regulator - 5V [package="TO220 [THT]"]
  C10 = Electrolytic Capacitor [capacitance=100µF package="100 mil [THT, electrolytic]"]
  Role_3 = songle relay
  R34 = Resistor [tolerance=±5% resistance=220 package=THT]
  Role_1 = songle relay
  D12 = Rectifier Diode [part_number=1N4001 package="300 mil [THT]"]
  C11 = Electrolytic Capacitor [capacitance=100nF package="100 mil [THT, electrolytic]"]
  R26 = Resistor [tolerance=±5% resistance=220 package=THT]
  R29 = Resistor [tolerance=±5% resistance=220 package=THT]
  R35 = Resistor [tolerance=±5% resistance=220 package=THT]
  LED8 = LED - 5mm [color="Green (555nm)" package="5 mm [THT]"]
  R36 = Resistor [tolerance=±5% resistance=220 package=THT]
  D8 = Rectifier Diode [part_number=1N4001 package="300 mil [THT]"]
  D13 = Rectifier Diode [part_number=1N4001 package="300 mil [THT]"]
  R32 = Resistor [tolerance=±5% resistance=220 package=THT]
  R16 = Resistor [tolerance=±5% resistance=220 package=THT]
  C12 = Electrolytic Capacitor [capacitance=1µF package="100 mil [THT, electrolytic]"]
  R28 = Resistor [tolerance=±5% resistance=15k package=THT]
  R27 = Resistor [tolerance=±5% resistance=10k package=THT]
  Panel = screw terminal, 2 pins
  Akü_Giriş = screw terminal, 2 pins
  Role_2 = songle relay
  C8 = Capacitor [package=cap-pth-small2]
  12V_Çıkış = screw terminal, 2 pins
  U5 = Voltage Regulator - 5V [package="TO220 [THT]"]
  LED5 = LED - 5mm [color="Red (633nm)" package="5 mm [THT]"]
  R31 = Resistor [tolerance=±5% resistance=220 package=THT]
  5V- = Header 1 [package=1x01_offset]
  SD+ = Header 1 [package=1x01_offset]
  U4 = atmega328 [package=dip]
  XTAL2 = Crystal [frequency="16 Mhz" package=THT]
  LED12 = LED - 5mm [color="Red (633nm)" package="5 mm [THT]"]
  C13 = Electrolytic Capacitor [capacitance=1µF package="100 mil [THT, electrolytic]"]
  Q9 = NPN-Transistor [package="TO92 [THT]"]
  R24 = Resistor [tolerance=±5% resistance=220 package=THT]
  12V_Çıkış_Motor = screw terminal, 2 pins
  LED9 = LED - 5mm [color="Yellow (585nm)" package="5 mm [THT]"]
  Q10 = NPN-Transistor [package="TO92 [THT]"]
  R10 = Resistor [tolerance=±5% resistance=100 package=THT]
  R33 = Resistor [tolerance=±5% resistance=220 package=THT]
  LED11 = LED - 5mm [color="Red (633nm)" package="5 mm [THT]"]
  R15 = Resistor [tolerance=±5% resistance=220 package=THT]
  R30 = Resistor [tolerance=±5% resistance=220 package=THT]
  Buzzer- = Header 1 [package=1x01_offset]
  Buzzer+ = Header 1 [package=1x01_offset]

nets:
  N1: R25.Pin_0, LED9.cathode
  GND: R25.Pin_1, Q8.C, S6.leg1, 5V_Çıkış_Motor.pin2, 5V_Çıkış.pin2, C7.2, 12.GND, C10.-, C11.-, R26.Pin_1, R36.Pin_0, R32.Pin_0, C12.-, R27.Pin_0, Panel.pin2, Akü_Giriş.pin2, C8.1, 12V_Çıkış.pin2, U5.GND, 5V-.1, SD+.1, U4.GND, C13.-, Q9.C, R24.Pin_1, 12V_Çıkış_Motor.pin2, Q10.C, Buzzer-.1
  N2: 5V+.1, 5V_Çıkış_Motor.pin1, 5V_Çıkış.pin1
  N3: Q8.E, Role_1.COIL2, D8.anode, LED5.cathode
  N4: Q8.B, R16.Pin_1
  N5: SD-.1, Role_1.A, R28.Pin_0, 12V_Çıkış.pin1, 12V_Çıkış_Motor.pin1
  N6: LED10.cathode, R26.Pin_0
  N7: LED10.anode, U4.D13
  N8: S6.leg0, U4.RESET, R10.Pin_1
  N9: S7.COM, C10.+, Role_1.CT, U5.input_voltage
  N10: S7.L2, Akü_Giriş.pin1
  N11: C7.1, U4.XLAT1, XTAL2.pin_1
  N12: 12.input_voltage, Role_3.B, Role_2.B, C13.+
  N13: 12.output_voltage, C12.+
  N14: Role_3.COIL1, Role_1.COIL1, D12.cathode, R29.Pin_1, D8.cathode, D13.cathode, Role_2.COIL1, R33.Pin_1, R15.Pin_1
  N15: Role_3.COIL2, D13.anode, LED12.cathode, Q10.E
  N16: Role_3.CT, Role_1.B
  N17: Role_3.A, R35.Pin_1
  N18: R34.Pin_0, U4.D4
  N19: R34.Pin_1, Q10.B
  N20: D12.anode, Role_2.COIL2, Q9.E, LED11.cathode
  N21: C11.+, U5.output_voltage, U4.VCC, U4.AVCC, R10.Pin_0
  N22: R29.Pin_0, LED11.anode
  N23: R35.Pin_0, R36.Pin_1, U4.A2
  N24: LED8.cathode, R24.Pin_0
  N25: LED8.anode, U4.D11_(PWM)
  N26: R32.Pin_1, R31.Pin_1, U4.A1
  N27: R16.Pin_0, U4.D10_(PWM)
  N28: R28.Pin_1, R27.Pin_1, U4.A0
  N29: Panel.pin1, Role_2.CT
  N30: Role_2.A, R31.Pin_0
  N31: C8.2, U4.XLAT2, XTAL2.pin_0
  N32: LED5.anode, R15.Pin_0
  N33: U4.D7, R30.Pin_0, Buzzer+.1
  N34: U4.D12, LED9.anode
  N35: LED12.anode, R33.Pin_0
  N36: Q9.B, R30.Pin_1
