# Fritzing sketch Şarj İstasyonu (saved by Fritzing 0.9.2b)
breadboards: 3

parts:
  LiPo1 = screw terminal, 2 pins
  StepUp_IN_+ = Header 1 [package=1x01_offset]
  StepUp_IN_- = Header 1 [package=1x01_offset]
  Panel = screw terminal, 2 pins
  Eleman4 = songle relay
  Q5 = NPN-Transistor [package="TO92 [THT]"]
  D5 = Rectifier Diode [part_number=1N4001 package="300 mil [THT]"]
  R12 = Resistor [tolerance=±5% resistance=220 package=THT]
  LED2 = LED - 5mm [color="Red (633nm)" package="5 mm [THT]"]
  Eleman5 = songle relay
  Q6 = NPN-Transistor [package="TO92 [THT]"]
  D6 = Rectifier Diode [part_number=1N4001 package="300 mil [THT]"]
  R13 = Resistor [tolerance=±5% resistance=220 package=THT]
  Eleman6 = songle relay
  Q7 = NPN-Transistor [package="TO92 [THT]"]
  D7 = Rectifier Diode [part_number=1N4001 package="300 mil [THT]"]
  R14 = Resistor [tolerance=±5% resistance=220 package=THT]
  LED4 = LED - 5mm [color="Red (633nm)" package="5 mm [THT]"]
  Eleman7 = songle relay
  Q8 = NPN-Transistor [package="TO92 [THT]"]
  D8 = Rectifier Diode [part_number=1N4001 package="300 mil [THT]"]
  R15 = Resistor [tolerance=±5% resistance=220 package=THT]
  LED5 = LED - 5mm [color="Red (633nm)" package="5 mm [THT]"]
  S6 = Pushbutton [package=THT]
  XTAL2 = Crystal [frequency="16 Mhz" package=THT]
  Atmega_Guc = screw terminal, 2 pins
  U4 = atmega328 [package=dip]
  C7 = Capacitor [package=cap-pth-small2]
  C8 = Capacitor [package=cap-pth-small2]
  R10 = Resistor [tolerance=±5% resistance=100 package=THT]
  LiPo2 = screw terminal, 2 pins
  LED3 = LED - 5mm [color="Red (633nm)" package="5 mm [THT]"]
  Pi_Çıkış = screw terminal, 2 pins
  StepUp_OUT_- = Header 1 [package=1x01_offset]
  StepUp_OUT_+ = Header 1 [package=1x01_offset]
  R16 = Resistor [tolerance=±5% resistance=220 package=THT]
  R17 = Resistor [tolerance=±5% resistance=220 package=THT]
  R18 = Resistor [tolerance=±5% resistance=220 package=THT]
  R19 = Resistor [tolerance=±5% resistance=220 package=THT]
  S7 = Toggle Switch [package=THT]
  S8 = Toggle Switch [package=THT]
  Eleman8 = songle relay
  Q9 = NPN-Transistor [package="TO92 [THT]"]
  D9 = Rectifier Diode [part_number=1N4001 package="300 mil [THT]"]
  R20 = Resistor [tolerance=±5% resistance=220 package=THT]
  LED6 = LED - 5mm [color="Red (633nm)" package="5 mm [THT]"]
  R21 = Resistor [tolerance=±5% resistance=220 package=THT]
  Akü_Giriş = screw terminal, 2 pins
  Akü_Şarj = screw terminal, 2 pins
  Motor_12V = screw terminal, 2 pins
  12V- = Header 1 [package=1x01_offset]
  12V+ = Header 1 [package=1x01_offset]
  5V+ = Header 1 [package=1x01_offset]
  5V- = Header 1 [package=1x01_offset]
  5V_Çıkış = screw terminal, 2 pins
  C9 = Electrolytic Capacitor [capacitance=1µF package="100 mil [THT, electrolytic]"]

nets:
  N1: LiPo1.pin1, S8.L2
  N2: LiPo1.pin2, StepUp_IN_-.1, Panel.pin2, Q5.C, Q6.C, Q7.C, Q8.C, S6.leg1, Atmega_Guc.pin2, U4.GND, C7.2, C8.1, LiPo2.pin2, Pi_Çıkış.pin1, StepUp_OUT_-.1, Q9.C, Akü_Giriş.pin1, Akü_Şarj.pin2, Motor_12V.pin2, 12V+.1, 5V-.1, 5V_Çıkış.pin2, C9.+
  N3: StepUp_IN_+.1, Eleman4.B, Eleman7.B
  N4: Panel.pin1, Eleman5.B, Eleman6.B
  N5: Eleman4.COIL1, D5.cathode, R12.Pin_1, Eleman5.COIL1, D6.cathode, R13.Pin_1, Eleman6.COIL1, D7.cathode, R14.Pin_1, Eleman7.COIL1, D8.cathode, R15.Pin_1
  N6: Eleman4.COIL2, Q5.E, D5.anode, LED2.cathode
  N7: Eleman4.CT, Eleman5.CT, S8.COM
  N8: Q5.B, R19.Pin_1
  N9: R12.Pin_0, LED2.anode
  N10: Eleman5.COIL2, Q6.E, D6.anode, LED3.cathode
  N11: Q6.B, R18.Pin_1
  N12: R13.Pin_0, LED3.anode
  N13: Eleman6.COIL2, Q7.E, D7.anode, LED4.cathode
  N14: Eleman6.CT, Eleman7.CT, S7.COM
  N15: Q7.B, R17.Pin_1
  N16: R14.Pin_0, LED4.anode
  N17: Eleman7.COIL2, Q8.E, D8.anode, LED5.cathode
  N18: Q8.B, R16.Pin_1
  N19: R15.Pin_0, LED5.anode
  N20: S6.leg0, U4.RESET, R10.Pin_1
  N21: XTAL2.pin_0, U4.D5_(PWM), C8.2
  N22: XTAL2.pin_1, U4.XLAT1, C7.1
  N23: Atmega_Guc.pin1, U4.VCC, U4.AVCC, R10.Pin_0, C9.-
  N24: U4.D0_(RX), R16.Pin_0
  N25: U4.D1_(TX), R17.Pin_0
  N26: U4.D2, R18.Pin_0
  N27: U4.D3_(PWM), R19.Pin_0
  N28: U4.D4, R21.Pin_0
  N29: LiPo2.pin1, S7.L2
  N30: Pi_Çıkış.pin2, StepUp_OUT_+.1
  N31: Eleman8.B, Akü_Şarj.pin1
  N32: Eleman8.COIL1, Eleman8.A, D9.cathode, R20.Pin_1, Motor_12V.pin1, 12V-.1
  N33: Eleman8.COIL2, Q9.E, D9.anode, LED6.cathode
  N34: Eleman8.CT, Akü_Giriş.pin2
  N35: Q9.B, R21.Pin_1
  N36: R20.Pin_0, LED6.anode
  N37: 5V+.1, 5V_Çıkış.pin1

notes:
  StepDown
